# Fritzing sketch SEMEN-NOKIA-WATCH (saved by Fritzing 0.9.5d)

parts:
  LCD1 = LCD screen
  Part1 = Arduino Nano (Rev3.0)
  LCM1602_IIC1 = LCM1602 IIC [part_number="LCM1602 IIC" chip_label="LCM1602 IIC" package="DIP (Dual Inline) [THT]"]
  DS1302 = Real Time Clock Module - DS1302 RTC Breakout Board
  RE1 = Rotary Encoder [package=THT]
  S1 = Pushbutton [package="[THT]"]

nets:
  VSS: LCD1.VSS, LCM1602_IIC1.VSS
  VDD: LCD1.VDD, LCM1602_IIC1.VDD
  N1: LCD1.V0, LCM1602_IIC1.V0
  N2: LCD1.RS, LCM1602_IIC1.RS
  N3: LCD1.R/W, LCM1602_IIC1.RW
  N4: LCD1.E, LCM1602_IIC1.E
  N5: LCD1.DB0, LCM1602_IIC1.D0
  N6: LCD1.DB1, LCM1602_IIC1.D1
  N7: LCD1.DB2, LCM1602_IIC1.D2
  N8: LCD1.DB3, LCM1602_IIC1.D3
  N9: LCD1.DB4, LCM1602_IIC1.D4
  N10: LCD1.DB5, LCM1602_IIC1.D5
  N11: LCD1.DB6, LCM1602_IIC1.D6
  N12: LCD1.DB7, LCM1602_IIC1.D7
  N13: LCD1.LED+, LCM1602_IIC1.A
  N14: LCD1.LED-, LCM1602_IIC1.K
  GND: Part1.GND, LCM1602_IIC1.GND, DS1302.GND, RE1.EncoderPinC, S1.Pin_2
  N15: Part1.D2, RE1.EncoderPinB
  N16: Part1.D3, RE1.EncoderPinA
  N17: Part1.D4, S1.Pin_4
  N18: Part1.D8, DS1302.RST
  N19: Part1.D9, DS1302.CLK
  N20: Part1.D10, DS1302.DAT
  5V: Part1.5V, LCM1602_IIC1.VCC, DS1302.5V
  N21: Part1.A5, LCM1602_IIC1.SCL
  N22: Part1.A4, LCM1602_IIC1.SDA

custom parts:
  LCM1602 IIC: I2C-Module to use a 1602 or 2004 LCD on with the wire.h libory Serial LCD Modul
  Real Time Clock Module - DS1302 RTC Breakout Board: This a custom designed module for the DS1307 Real Time Clock. The module comes fully assembled and pre-programmed with the current time (ok, so it's our current time - MST). The included Lithium coin cell battery (CR1225 41mAh) will run the module for a minimum of 9 years (17 years typical) without external 5V power. The DS1307 is accessed via the I2C protocol. We've written a test-bed to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
